# Fritzing sketch Gardenr (saved by Fritzing 0.9.3b)
circuit board: 5.84359cm x 4.83459cm
breadboards: 1

parts:
  MCP3008 = MCP3008 [package=dil16]
  SHT-21 = female pin header, 4 pins [form="♀ (female)"]
  SOIL = female pin header, 3 pins [form="♀ (female)"]
  LCD = female pin header, 4 pins [form="♀ (female)"]

nets:
  N1: MCP3008.CH0, SOIL.pin1
  N2: MCP3008.DGND, SHT-21.pin4, SOIL.pin3, LCD.pin4
  N3: MCP3008.VREF, MCP3008.VDD
  N4: SHT-21.pin1, LCD.pin1
  N5: SHT-21.pin2, LCD.pin2
  N6: SOIL.pin2, LCD.pin3
